# Fritzing sketch schematic (saved by Fritzing 0.9.5d)
breadboards: 1

parts:
  Part1 = Adafruit PowerBoost 1000C [part_number="Adafruit #2465"]
  Part2 = Lithium Ion Battery Pack 3.7V 6600mAh [part_number=353]
  Part3 = Motor Driver 1A Dual TB6612FNG
  M1 = DC Motor
  M2 = DC Motor
  Mod1 = Raspberry Pi 4B  # not connected

nets:
  GND: Part1.GND, Part2.negative, Part3.GND
  vlipo: Part1.VLIPO, Part2.positive
  vbat: Part1.VBAT, Part3.VCC
  N1: Part3.B01, M2.pin_1
  N2: Part3.B02, M2.pin_2
  N3: Part3.A02, M1.pin_2
  N4: Part3.A01, M1.pin_1

custom parts:
  Adafruit PowerBoost 1000C: PowerBoost 1000C is the perfect power supply for your portable project! With a built-in load-sharing battery charger circuit, you'll be able to keep your power-hungry project running even while recharging the battery! This little DC/DC boost converter module can be powered by any 3.7V LiIon/LiPoly battery, and convert the battery output to 5.2V DC for running your 5V projects.
  Lithium Ion Battery Pack 3.7V 6600mAh: This lithium ion pack is made of 3 balanced 2200mAh cells for a total of 6600mA capacity! The cells are connected in parallel and spot-welded to a protection circuit that provides over-voltage, under-voltage and over-current protection. Each cell can provide 0.5C of current (1.1 A per) so all together the peak current you can draw is over 3.3 Amps. Note that these batteries are not designed to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
