# Fritzing sketch schematic (saved by Fritzing 0.9.5d)
circuit board: 8.46667cm x 5.64444cm
breadboards: 1

parts:
  Part1 = Adafruit PowerBoost 1000C [part_number="Adafruit #2465"]
  Part2 = Lithium Ion Battery Pack 3.7V 6600mAh [part_number=353]
  Part3 = Motor Driver 1A Dual TB6612FNG
  left_motor = DC Motor
  right_motor = DC Motor
  Mod1 = Raspberry Pi 4B

nets (from the schematic view):
  GND: Part1.GND, Part2.negative, Part3.GND, Mod1.GND
  5V: Part1.5.0V, Part3.VCC, Mod1.5V
  vlipo: Part1.VLIPO, Part2.positive, Part3.VM
  vbat: Part1.VBAT
  N1: Part3.B01, right_motor.pin_1
  N2: Part3.B02, right_motor.pin_2
  N3: Part3.A02, left_motor.pin_2
  N4: Part3.A01, left_motor.pin_1
  left_motor.speed: Part3.PWMA, Mod1.GPIO12
  left_motor.backward: Part3.AIN2, Mod1.GPIO20
  left_motor.forward: Part3.AIN1, Mod1.GPIO16
  motor_standby: Part3.STBY, Mod1.GPIO6
  right_motor.forward: Part3.BIN1, Mod1.GPIO19
  right_motor.backward: Part3.BIN2, Mod1.GPIO26
  right_motor.speed: Part3.PWMB, Mod1.GPIO13

custom parts:
  Adafruit PowerBoost 1000C: PowerBoost 1000C is the perfect power supply for your portable project! With a built-in load-sharing battery charger circuit, you'll be able to keep your power-hungry project running even while recharging the battery! This little DC/DC boost converter module can be powered by any 3.7V LiIon/LiPoly battery, and convert the battery output to 5.2V DC for running your 5V projects.
  Lithium Ion Battery Pack 3.7V 6600mAh: This lithium ion pack is made of 3 balanced 2200mAh cells for a total of 6600mA capacity! The cells are connected in parallel and spot-welded to a protection circuit that provides over-voltage, under-voltage and over-current protection. Each cell can provide 0.5C of current (1.1 A per) so all together the peak current you can draw is over 3.3 Amps. Note that these batteries are not designed to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
